// Logisim project 数值逻辑实验报告大作业.circ as structural Verilog: 1 circuit, main circuit main
module main (
  input  a,
  input  b,
  input  c
);

  wire and_1_out, and_2_out, and_3_out, and_4_out, and_5_out, and_6_out, clock_1_out, d_ff_1_q, d_ff_2_q,
       d_ff_3_q, d_ff_4_q, d_ff_5_q, not_1_out, not_2_out, not_3_out;

  Clock clock_1 (.out(clock_1_out));
  and and_1 (and_1_out, d_ff_1_q, d_ff_2_q, d_ff_3_q, d_ff_4_q, d_ff_5_q);
  not not_1 (not_1_out, a);
  not not_2 (not_2_out, b);
  not not_3 (not_3_out, c);
  and and_2 (and_2_out, and_1_out, not_1_out, not_2_out, not_3_out);
  D_Flip_Flop d_ff_1 (.clk(clock_1_out), .D(and_2_out), .Q(d_ff_1_q));  // open: Qn, preset, en, reset
  and and_3 (and_3_out, not_1_out, not_2_out, and_1_out, c);
  D_Flip_Flop d_ff_2 (.clk(clock_1_out), .D(and_3_out), .Q(d_ff_2_q));  // open: Qn, preset, en, reset
  and and_4 (and_4_out, not_1_out, and_1_out, b, not_3_out);
  D_Flip_Flop d_ff_3 (.clk(clock_1_out), .D(and_4_out), .Q(d_ff_3_q));  // open: Qn, preset, en, reset
  D_Flip_Flop d_ff_4 (.clk(clock_1_out), .D(and_5_out), .Q(d_ff_4_q));  // open: Qn, preset, en, reset
  and and_5 (and_5_out, not_1_out, b, and_1_out, c);
  and and_6 (and_6_out, a, not_2_out, and_1_out, not_3_out);
  D_Flip_Flop d_ff_5 (.clk(clock_1_out), .D(and_6_out), .Q(d_ff_5_q));  // open: Qn, preset, en, reset

  // Notes on the sheet:
  //   Q4
  //   Q3
  //   Q2
  //   Q1
  //   Q0
endmodule
